// Logisim project Boba Vending Machine.circ as structural Verilog: 10 circuits, main circuit main
module main (
  output [2:0] out_1,
  output out_2
);

  wire button_1_out, button_2_out, button_3_out, button_4_out, button_5_out, button_6_out, button_7_out,
       button_8_out, button_9_out, button_10_out, button_11_out, button_12_out, clock_1_out, Clr_out;
  wire [3:0] n12_bit_bcd_converter_1_hundreds, n12_bit_bcd_converter_1_ones, n12_bit_bcd_converter_1_tens,
       n12_bit_bcd_converter_1_thousands, n12_bit_bcd_converter_2_hundreds, n12_bit_bcd_converter_2_ones,
       n12_bit_bcd_converter_2_tens, n12_bit_bcd_converter_2_thousands, n12_bit_bcd_converter_3_hundreds,
       n12_bit_bcd_converter_3_ones, n12_bit_bcd_converter_3_tens, n12_bit_bcd_converter_3_thousands;
  wire [11:0] flavor_input_1_price, money_input_1_out_11, money_input_1_out_12;

  LED Not_Enough_Money ();  // open: in
  Button button_1 (.out(button_1_out));
  Button button_2 (.out(button_2_out));
  Button button_3 (.out(button_3_out));
  Button button_4 (.out(button_4_out));
  Button button_5 (.out(button_5_out));
  Button button_6 (.out(button_6_out));
  Button button_7 (.out(button_7_out));
  Button button_8 (.out(button_8_out));
  Button button_9 (.out(button_9_out));
  Button button_10 (.out(button_10_out));
  LED led_1 ();  // open: in
  Button button_11 (.out(button_11_out));
  LED led_2 ();  // open: in
  Button button_12 (.out(button_12_out));
  LED led_3 ();  // open: in
  Money_Input money_input_1 (
    .Reset(Clr_out), ._1(button_1_out), ._5(button_2_out), ._10(button_3_out), ._25(button_4_out),
    ._50(button_5_out), ._1_2(button_6_out), ._5_2(button_7_out), ._10_2(button_8_out), ._20(button_9_out),
    .out_11(money_input_1_out_11), .out_12(money_input_1_out_12));
  Button Clr (.out(Clr_out));
  Button Buy ();  // open: out
  Flavor_Input flavor_input_1 (
    .in_1(button_10_out), .Price(flavor_input_1_price), .Flavor(out_1), .in_2(button_11_out),
    .in_3(button_12_out), .in_4(Clr_out));
  Hex_Digit_Display hex_digit_display_1 (.value(n12_bit_bcd_converter_1_hundreds));  // open: dp
  Hex_Digit_Display hex_digit_display_2 (.value(n12_bit_bcd_converter_1_thousands));  // open: dp
  _12_bit_BCD_Converter u_12_bit_bcd_converter_1 (
    .Input(money_input_1_out_11), .Thousands(n12_bit_bcd_converter_1_thousands),
    .Hundreds(n12_bit_bcd_converter_1_hundreds), .Tens(n12_bit_bcd_converter_1_tens),
    .Ones(n12_bit_bcd_converter_1_ones));
  Hex_Digit_Display hex_digit_display_3 (.value(n12_bit_bcd_converter_1_ones));  // open: dp
  Hex_Digit_Display hex_digit_display_4 (.value(n12_bit_bcd_converter_1_tens));  // open: dp
  Hex_Digit_Display hex_digit_display_5 (.value(n12_bit_bcd_converter_2_thousands));  // open: dp
  Hex_Digit_Display hex_digit_display_6 (.value(n12_bit_bcd_converter_2_hundreds));  // open: dp
  _12_bit_BCD_Converter u_12_bit_bcd_converter_2 (
    .Input(flavor_input_1_price), .Thousands(n12_bit_bcd_converter_2_thousands),
    .Hundreds(n12_bit_bcd_converter_2_hundreds), .Tens(n12_bit_bcd_converter_2_tens),
    .Ones(n12_bit_bcd_converter_2_ones));
  Hex_Digit_Display hex_digit_display_7 (.value(n12_bit_bcd_converter_2_tens));  // open: dp
  Hex_Digit_Display hex_digit_display_8 (.value(n12_bit_bcd_converter_2_ones));  // open: dp
  LED led_4 (.in(out_1[0]));
  LED led_5 (.in(out_1[1]));
  LED led_6 (.in(out_1[2]));
  Hex_Digit_Display hex_digit_display_9 (.value(n12_bit_bcd_converter_3_thousands));  // open: dp
  Hex_Digit_Display hex_digit_display_10 (.value(n12_bit_bcd_converter_3_tens));  // open: dp
  Hex_Digit_Display hex_digit_display_11 (.value(n12_bit_bcd_converter_3_hundreds));  // open: dp
  _12_bit_BCD_Converter u_12_bit_bcd_converter_3 (
    .Input(money_input_1_out_12), .Thousands(n12_bit_bcd_converter_3_thousands),
    .Hundreds(n12_bit_bcd_converter_3_hundreds), .Tens(n12_bit_bcd_converter_3_tens),
    .Ones(n12_bit_bcd_converter_3_ones));
  Hex_Digit_Display hex_digit_display_12 (.value(n12_bit_bcd_converter_3_ones));  // open: dp
  Clock clock_1 (.out(clock_1_out));
  Money_Dispense money_dispense_1 (
    .How_many_1(n12_bit_bcd_converter_3_ones), .How_many_10(n12_bit_bcd_converter_3_tens),
    .How_many__1(n12_bit_bcd_converter_3_hundreds), .How_many__10(n12_bit_bcd_converter_3_thousands),
    .out_7(out_2), .Clock(clock_1_out));  // open: in_2, out_8, out_9, out_10

  // Notes on the sheet:
  //   Money Input
  //   Balance:
  //   Price:
  //   Change:
endmodule

module Flavor_Input (
  input  in_1,
  input  in_2,
  input  in_3,
  input  in_4,
  output [11:0] Price,
  output [2:0] Flavor
);

  wire comparator_1_eq, not_1_out;

  Comparator #(.width(3)) comparator_1 (.a({in_3, in_2, in_1}), .b(3'b000), .eq(comparator_1_eq));  // open: gt, lt
  not not_1 (not_1_out, comparator_1_eq);
  Register #(.width(3)) register_1 (.D({in_3, in_2, in_1}), .en(not_1_out), .Q(Flavor), .clk(not_1_out), .clr(in_4));
  Flavor_State flavor_state_1 (
    .a(Flavor[0]), .b(Flavor[1]), .c(Flavor[2]), .x(Price[11]), .y(Price[10]), .z(Price[9]), .u(Price[8]),
    .v(Price[7]), .w(Price[6]), .s(Price[5]), .t(Price[4]), .x2(Price[3]), .x3(Price[2]), .x4(Price[1]),
    .x5(Price[0]));
endmodule

module Flavor_State (
  input  a,
  input  b,
  input  c,
  output x,
  output y,
  output z,
  output u,
  output v,
  output w,
  output s,
  output t,
  output x2,
  output x3,
  output x4,
  output x5
);

  wire and_2_out, and_3_out, and_5_out, and_6_out, and_7_out, and_10_out, and_11_out, and_12_out, and_13_out,
       not_1_out, not_2_out, not_3_out, not_4_out, not_5_out, not_6_out, not_7_out, not_8_out, not_9_out,
       not_10_out, not_11_out, not_12_out, not_13_out, not_14_out, not_15_out, not_16_out, not_17_out,
       not_18_out, not_19_out, not_20_out, not_21_out, not_22_out, not_23_out, not_24_out, not_25_out,
       not_26_out, not_27_out, not_28_out;

  not not_1 (not_1_out, a);
  not not_2 (not_2_out, b);
  not not_3 (not_3_out, a);
  not not_4 (not_4_out, c);
  not not_5 (not_5_out, b);
  not not_6 (not_6_out, c);
  not not_7 (not_7_out, a);
  not not_8 (not_8_out, c);
  not not_9 (not_9_out, a);
  not not_10 (not_10_out, b);
  not not_11 (not_11_out, a);
  not not_12 (not_12_out, c);
  not not_13 (not_13_out, b);
  not not_14 (not_14_out, c);
  not not_15 (not_15_out, b);
  not not_16 (not_16_out, c);
  not not_17 (not_17_out, a);
  not not_18 (not_18_out, b);
  not not_19 (not_19_out, a);
  not not_20 (not_20_out, b);
  not not_21 (not_21_out, b);
  not not_22 (not_22_out, c);
  not not_23 (not_23_out, a);
  not not_24 (not_24_out, c);
  not not_25 (not_25_out, b);
  not not_26 (not_26_out, c);
  not not_27 (not_27_out, b);
  not not_28 (not_28_out, c);
  and and_1 (y, not_1_out, not_2_out, c);
  and and_2 (and_2_out, not_3_out, b, not_4_out);
  and and_3 (and_3_out, a, not_5_out, not_6_out);
  and and_4 (u, not_7_out, b, not_8_out);
  and and_5 (and_5_out, not_9_out, not_10_out, c);
  and and_6 (and_6_out, not_11_out, b, not_12_out);
  and and_7 (and_7_out, a, not_13_out, not_14_out);
  and and_8 (w, a, not_15_out, not_16_out);
  and and_9 (s, not_17_out, not_18_out, c);
  and and_10 (and_10_out, not_19_out, not_20_out, c);
  and and_11 (and_11_out, a, not_21_out, not_22_out);
  and and_12 (and_12_out, not_23_out, b, not_24_out);
  and and_13 (and_13_out, a, not_25_out, not_26_out);
  and and_14 (x5, a, not_27_out, not_28_out);
  or or_1 (z, and_2_out, and_3_out);
  or or_2 (v, and_5_out, and_6_out, and_7_out);
  or or_3 (t, and_10_out, and_11_out);
  or or_4 (x3, and_12_out, and_13_out);

  assign x = 1'b0;
  assign x2 = 1'b0;
  assign x4 = 1'b0;
endmodule

// Super adder
module _12_bit_super_adder (
  input  [11:0] in_1,
  input  [11:0] in_2,
  input  [11:0] in_3,
  input  [11:0] in_4,
  input  [11:0] in_5,
  input  [11:0] in_6,
  input  [11:0] in_7,
  input  [11:0] in_8,
  input  [11:0] in_9,
  output [11:0] Total,
  output out_11
);

  wire [11:0] adder_1_out, adder_2_out, adder_3_out, adder_4_out, adder_5_out, adder_6_out, adder_7_out;

  Adder #(.width(12)) adder_1 (.a(in_1), .b(in_2), .out(adder_1_out));  // open: cin, cout
  Adder #(.width(12)) adder_2 (.a(in_3), .b(in_4), .out(adder_2_out));  // open: cin, cout
  Adder #(.width(12)) adder_3 (.a(in_5), .b(in_6), .out(adder_3_out));  // open: cin, cout
  Adder #(.width(12)) adder_4 (.a(in_7), .b(in_8), .out(adder_4_out));  // open: cin, cout
  Adder #(.width(12)) adder_5 (.a(adder_1_out), .b(adder_2_out), .out(adder_5_out));  // open: cin, cout
  Adder #(.width(12)) adder_6 (.a(adder_3_out), .b(adder_4_out), .out(adder_6_out));  // open: cin, cout
  Adder #(.width(12)) adder_7 (.a(adder_5_out), .b(adder_6_out), .out(adder_7_out));  // open: cin, cout
  Adder #(.width(12)) adder_8 (.a(adder_7_out), .b(in_9), .out(Total));  // open: cin, cout
  Comparator #(.width(12)) comparator_1 (.a(Total), .b({12{1'b0}}), .gt(out_11));  // open: eq, lt
endmodule

module _12_bit_BCD_Converter (
  input  [11:0] Input,
  output [3:0] Thousands,
  output [3:0] Hundreds,
  output [3:0] Tens,
  output [3:0] Ones
);

  wire comparator_1_lt, comparator_2_lt, comparator_3_lt, comparator_4_lt, comparator_5_lt, comparator_6_lt,
       comparator_7_lt, comparator_8_lt, comparator_9_lt, comparator_10_lt, comparator_11_lt,
       comparator_12_lt, comparator_13_lt, comparator_14_lt, comparator_15_lt, comparator_16_lt,
       comparator_17_lt, comparator_18_lt, comparator_19_lt;
  wire [0:0] adder_1_out_2, adder_2_out, adder_4_out_2;
  wire [1:1] not_1_out, not_2_out, not_3_out, not_4_out, not_5_out, not_6_out, not_7_out, not_8_out,
       not_9_out, not_10_out, not_11_out, not_12_out, not_13_out, not_14_out, not_15_out, not_16_out,
       not_17_out, not_18_out, not_19_out;
  wire [2:0] adder_11_out_2, adder_14_out_2;
  wire [3:0] adder_14_out, adder_16_out;
  wire [3:1] adder_1_out, adder_2_out_3, adder_5_out, adder_11_out, adder_12_out, adder_13_out;
  wire [11:0] adder_3_out, adder_4_out, adder_8_out, adder_15_out, adder_17_out, adder_18_out, adder_19_out;
  wire [11:1] adder_7_out;
  wire [11:3] adder_5_out_2;
  wire [11:4] adder_2_out_2, adder_6_out, adder_9_out, adder_10_out, adder_11_out_3, adder_12_out_2,
       adder_13_out_2, adder_14_out_3, adder_16_out_2;
  wire [11:11] adder_1_out_3;

  not not_1 (not_1_out[1], comparator_1_lt);
  not not_2 (not_2_out[1], comparator_2_lt);
  not not_3 (not_3_out[1], comparator_3_lt);
  not not_4 (not_4_out[1], comparator_4_lt);
  not not_5 (not_5_out[1], comparator_5_lt);
  not not_6 (not_6_out[1], comparator_6_lt);
  Comparator #(.width(12), .mode("unsigned")) comparator_1 (
    .a({{8{1'b0}}, adder_17_out[2:0], Input[4]}), .b(12'h5), .lt(comparator_1_lt));  // open: gt, eq
  Adder #(.width(12)) adder_1 (
    .a({{8{1'b0}}, adder_17_out[2:0], Input[4]}), .b({{10{1'b0}}, {2{not_1_out[1]}}}),
    .out({{8{adder_1_out_3[11]}}, adder_1_out_2[0], adder_1_out}));  // open: cin, cout
  Comparator #(.width(12), .mode("unsigned")) comparator_2 (
    .a({{8{1'b0}}, adder_18_out[2:0], adder_1_out_2[0]}), .b(12'h5), .lt(comparator_2_lt));  // open: gt, eq
  Adder #(.width(12)) adder_2 (
    .a({{8{1'b0}}, adder_18_out[2:0], adder_1_out_2[0]}), .b({{10{1'b0}}, {2{not_2_out[1]}}}),
    .out({adder_2_out_2, adder_2_out[0], adder_2_out_3}));  // open: cin, cout
  Comparator #(.width(12), .mode("unsigned")) comparator_3 (
    .a({{8{1'b0}}, adder_1_out, Input[3]}), .b(12'h5), .lt(comparator_3_lt));  // open: gt, eq
  Adder #(.width(12)) adder_3 (
    .a({{8{1'b0}}, adder_1_out, Input[3]}), .b({{10{1'b0}}, {2{not_3_out[1]}}}), .out(adder_3_out));  // open: cin, cout
  Comparator #(.width(12), .mode("unsigned")) comparator_4 (
    .a({{8{1'b0}}, adder_2_out_3, adder_3_out[3]}), .b(12'h5), .lt(comparator_4_lt));  // open: gt, eq
  Adder #(.width(12)) adder_4 (
    .a({{8{1'b0}}, adder_2_out_3, adder_3_out[3]}), .b({{10{1'b0}}, {2{not_4_out[1]}}}),
    .out({adder_4_out[11:4], adder_4_out_2[0], adder_4_out[2:0]}));  // open: cin, cout
  Comparator #(.width(12), .mode("unsigned")) comparator_5 (
    .a({{8{1'b0}}, adder_3_out[2:0], Input[2]}), .b(12'h5), .lt(comparator_5_lt));  // open: gt, eq
  Adder #(.width(12)) adder_5 (
    .a({{8{1'b0}}, adder_3_out[2:0], Input[2]}), .b({{10{1'b0}}, {2{not_5_out[1]}}}),
    .out({adder_5_out_2, adder_5_out}));  // open: cin, cout
  Comparator #(.width(12), .mode("unsigned")) comparator_6 (
    .a({{8{1'b0}}, adder_8_out[2:0], adder_4_out_2[0]}), .b(12'h5), .lt(comparator_6_lt));  // open: gt, eq
  Adder #(.width(12)) adder_6 (
    .a({{8{1'b0}}, adder_8_out[2:0], adder_4_out_2[0]}), .b({{10{1'b0}}, {2{not_6_out[1]}}}),
    .out({adder_6_out, Thousands[0], Hundreds[3:1]}));  // open: cin, cout
  not not_7 (not_7_out[1], comparator_7_lt);
  not not_8 (not_8_out[1], comparator_8_lt);
  not not_9 (not_9_out[1], comparator_9_lt);
  not not_10 (not_10_out[1], comparator_10_lt);
  not not_11 (not_11_out[1], comparator_11_lt);
  not not_12 (not_12_out[1], comparator_12_lt);
  not not_13 (not_13_out[1], comparator_13_lt);
  not not_14 (not_14_out[1], comparator_14_lt);
  not not_15 (not_15_out[1], comparator_15_lt);
  not not_16 (not_16_out[1], comparator_16_lt);
  not not_17 (not_17_out[1], comparator_17_lt);
  not not_18 (not_18_out[1], comparator_18_lt);
  not not_19 (not_19_out[1], comparator_19_lt);
  Comparator #(.width(12), .mode("unsigned")) comparator_7 (
    .a({{11{1'b0}}, adder_19_out[3]}), .b(12'h5), .lt(comparator_7_lt));  // open: gt, eq
  Adder #(.width(12)) adder_7 (
    .a({{11{1'b0}}, adder_19_out[3]}), .b({{10{1'b0}}, {2{not_7_out[1]}}}), .out({adder_7_out, Thousands[2]}));  // open: cin, cout
  Comparator #(.width(12), .mode("unsigned")) comparator_8 (
    .a({{8{1'b0}}, adder_19_out[2:0], adder_2_out[0]}), .b(12'h5), .lt(comparator_8_lt));  // open: gt, eq
  Adder #(.width(12)) adder_8 (
    .a({{8{1'b0}}, adder_19_out[2:0], adder_2_out[0]}), .b({{10{1'b0}}, {2{not_8_out[1]}}}),
    .out({adder_8_out[11:4], Thousands[1], adder_8_out[2:0]}));  // open: cin, cout
  Comparator #(.width(12), .mode("unsigned")) comparator_9 (
    .a({{8{1'b0}}, adder_4_out[2:0], adder_5_out_2[3]}), .b(12'h5), .lt(comparator_9_lt));  // open: gt, eq
  Adder #(.width(12)) adder_9 (
    .a({{8{1'b0}}, adder_4_out[2:0], adder_5_out_2[3]}), .b({{10{1'b0}}, {2{not_9_out[1]}}}),
    .out({adder_9_out, Hundreds[0], Tens[3:1]}));  // open: cin, cout
  Comparator #(.width(12), .mode("unsigned")) comparator_10 (
    .a({{8{1'b0}}, adder_5_out, Input[1]}), .b(12'h5), .lt(comparator_10_lt));  // open: gt, eq
  Adder #(.width(12)) adder_10 (
    .a({{8{1'b0}}, adder_5_out, Input[1]}), .b({{10{1'b0}}, {2{not_10_out[1]}}}),
    .out({adder_10_out, Tens[0], Ones[3:1]}));  // open: cin, cout
  Comparator #(.width(12), .mode("unsigned")) comparator_11 (
    .a({{9{1'b0}}, Input[11:9]}), .b(12'h5), .lt(comparator_11_lt));  // open: gt, eq
  Adder #(.width(12)) adder_11 (
    .a({{9{1'b0}}, Input[11:9]}), .b({{10{1'b0}}, {2{not_11_out[1]}}}),
    .out({adder_11_out_3, adder_11_out_2[2], adder_11_out}));  // open: cin, cout
  Comparator #(.width(12), .mode("unsigned")) comparator_12 (
    .a({{8{1'b0}}, adder_11_out, Input[8]}), .b(12'h5), .lt(comparator_12_lt));  // open: gt, eq
  Adder #(.width(12)) adder_12 (
    .a({{8{1'b0}}, adder_11_out, Input[8]}), .b({{10{1'b0}}, {2{not_12_out[1]}}}),
    .out({adder_12_out_2, adder_11_out_2[1], adder_12_out}));  // open: cin, cout
  Comparator #(.width(12), .mode("unsigned")) comparator_13 (
    .a({{8{1'b0}}, adder_12_out, Input[7]}), .b(12'h5), .lt(comparator_13_lt));  // open: gt, eq
  Adder #(.width(12)) adder_13 (
    .a({{8{1'b0}}, adder_12_out, Input[7]}), .b({{10{1'b0}}, {2{not_13_out[1]}}}),
    .out({adder_13_out_2, adder_11_out_2[0], adder_13_out}));  // open: cin, cout
  Comparator #(.width(12), .mode("unsigned")) comparator_14 (
    .a({{9{1'b0}}, adder_11_out_2}), .b(12'h5), .lt(comparator_14_lt));  // open: gt, eq
  Adder #(.width(12)) adder_14 (
    .a({{9{1'b0}}, adder_11_out_2}), .b({{10{1'b0}}, {2{not_14_out[1]}}}),
    .out({adder_14_out_3, adder_14_out_2[2], adder_14_out[3:1]}));  // open: cin, cout
  Comparator #(.width(12), .mode("unsigned")) comparator_15 (
    .a({{8{1'b0}}, adder_13_out, Input[6]}), .b(12'h5), .lt(comparator_15_lt));  // open: gt, eq
  Adder #(.width(12)) adder_15 (
    .a({{8{1'b0}}, adder_13_out, Input[6]}), .b({{10{1'b0}}, {2{not_15_out[1]}}}),
    .out({adder_15_out[11:4], adder_14_out[0], adder_15_out[2:0]}));  // open: cin, cout
  Comparator #(.width(12), .mode("unsigned")) comparator_16 (
    .a({{8{1'b0}}, adder_14_out}), .b(12'h5), .lt(comparator_16_lt));  // open: gt, eq
  Adder #(.width(12)) adder_16 (
    .a({{8{1'b0}}, adder_14_out}), .b({{10{1'b0}}, {2{not_16_out[1]}}}),
    .out({adder_16_out_2, adder_14_out_2[1], adder_16_out[3:1]}));  // open: cin, cout
  Comparator #(.width(12), .mode("unsigned")) comparator_17 (
    .a({{8{1'b0}}, adder_15_out[2:0], Input[5]}), .b(12'h5), .lt(comparator_17_lt));  // open: gt, eq
  Adder #(.width(12)) adder_17 (
    .a({{8{1'b0}}, adder_15_out[2:0], Input[5]}), .b({{10{1'b0}}, {2{not_17_out[1]}}}),
    .out({adder_17_out[11:4], adder_16_out[0], adder_17_out[2:0]}));  // open: cin, cout
  Comparator #(.width(12), .mode("unsigned")) comparator_18 (
    .a({{8{1'b0}}, adder_16_out}), .b(12'h5), .lt(comparator_18_lt));  // open: gt, eq
  Adder #(.width(12)) adder_18 (
    .a({{8{1'b0}}, adder_16_out}), .b({{10{1'b0}}, {2{not_18_out[1]}}}),
    .out({{8{adder_18_out[11]}}, adder_14_out_2[0], adder_18_out[2:0]}));  // open: cin, cout
  Comparator #(.width(12), .mode("unsigned")) comparator_19 (
    .a({{9{1'b0}}, adder_14_out_2}), .b(12'h5), .lt(comparator_19_lt));  // open: gt, eq
  Adder #(.width(12)) adder_19 (
    .a({{9{1'b0}}, adder_14_out_2}), .b({{10{1'b0}}, {2{not_19_out[1]}}}), .out(adder_19_out));  // open: cin, cout
  Hex_Digit_Display hex_digit_display_1 (.value({1'b0, Thousands[2:0]}));  // open: dp
  Hex_Digit_Display hex_digit_display_2 (.value(Hundreds));  // open: dp
  Hex_Digit_Display hex_digit_display_3 (.value({Ones[3:1], Input[0]}));  // open: dp
  Hex_Digit_Display hex_digit_display_4 (.value(Tens));  // open: dp

  assign Ones[0] = Input[0];
  assign Thousands[3] = 1'b0;
  // also tied to GND on the sheet: {adder_1_out_3[11], adder_18_out[11]}

  // Notes on the sheet:
  //   Tens
  //   Hundreds
  //   Hundreds
  //   Thousands
  //   Thousands
  //   Ones
  //   Ones
  //   Ones
  //   Tens
  //   Ones
  //   Tens
  //   Ones
  //   Tens
  //   Ones
  //   Ones
  //   Tens
  //   Tens
  //   Hundreds
  //   Hundreds
  //   Ones
  //   Ones
  //   Tens
  //   Tens
  //   Ones
  //   Ones
endmodule

module calc_change (
  input  [11:0] in_1,
  input  [11:0] in_2,
  output [11:0] out_3
);

  Subtractor #(.width(12)) subtractor_1 (.a(in_1), .b(in_2), .out(out_3));  // open: bin, bout
endmodule

module Money_Dispense (
  input  [3:0] How_many_1,
  input  in_2,
  input  Clock,
  input  [3:0] How_many_10,
  input  [3:0] How_many__1,
  input  [3:0] How_many__10,
  output out_7,
  output out_8,
  output out_9,
  output out_10
);

  wire comparator_1_eq, comparator_2_eq, comparator_3_eq, comparator_4_eq, not_2_out, not_3_out, not_4_out,
       not_5_out;
  wire [0:0] not_1_out;
  wire [3:0] multiplexer_1_out, multiplexer_2_out, multiplexer_3_out, multiplexer_4_out, register_1_q,
       register_2_q, register_3_q, register_4_q, subtractor_1_out, subtractor_2_out, subtractor_3_out,
       subtractor_4_out;

  Multiplexer #(.width(4)) multiplexer_1 (
    .in0(register_1_q), .in1(How_many_10), .out(multiplexer_1_out), .sel(comparator_2_eq), .en(1'b1));
  Multiplexer #(.width(4)) multiplexer_2 (
    .in0(register_2_q), .in1(How_many_1), .out(multiplexer_2_out), .sel(comparator_1_eq), .en(1'b1));
  Multiplexer #(.width(4)) multiplexer_3 (
    .in0(register_3_q), .in1(How_many__1), .out(multiplexer_3_out), .sel(comparator_3_eq), .en(1'b1));
  Multiplexer #(.width(4)) multiplexer_4 (
    .in0(register_4_q), .in1(How_many__10), .out(multiplexer_4_out), .sel(comparator_4_eq), .en(1'b1));
  Subtractor #(.width(4)) subtractor_1 (
    .a(multiplexer_2_out), .b({3'b000, not_1_out[0]}), .out(subtractor_1_out));  // open: bin, bout
  not not_1 (not_1_out[0], comparator_1_eq);
  Subtractor #(.width(4)) subtractor_2 (.a(multiplexer_1_out), .b(4'b0001), .out(subtractor_2_out));  // open: bin, bout
  Register #(.width(4)) register_1 (.D(subtractor_2_out), .en(1'b1), .Q(register_1_q), .clk(Clock), .clr(in_2));
  Subtractor #(.width(4)) subtractor_3 (.a(multiplexer_3_out), .b(4'b0001), .out(subtractor_3_out));  // open: bin, bout
  Subtractor #(.width(4)) subtractor_4 (.a(multiplexer_4_out), .b(4'b0001), .out(subtractor_4_out));  // open: bin, bout
  Register #(.width(4)) register_2 (.D(subtractor_1_out), .en(1'b1), .Q(register_2_q), .clk(Clock), .clr(in_2));
  Register #(.width(4)) register_3 (.D(subtractor_3_out), .en(1'b1), .Q(register_3_q), .clk(Clock), .clr(in_2));
  Register #(.width(4)) register_4 (.D(subtractor_4_out), .en(1'b1), .Q(register_4_q), .clk(Clock), .clr(in_2));
  Comparator #(.width(4)) comparator_1 (.a(register_2_q), .b(4'b0000), .eq(comparator_1_eq));  // open: gt, lt
  not not_2 (not_2_out, comparator_2_eq);
  Comparator #(.width(4)) comparator_2 (.a(register_1_q), .b(4'b0000), .eq(comparator_2_eq));  // open: gt, lt
  not not_3 (not_3_out, comparator_1_eq);
  and and_1 (out_8, not_2_out, Clock);
  not not_4 (not_4_out, comparator_3_eq);
  Comparator #(.width(4)) comparator_3 (.a(register_3_q), .b(4'b0000), .eq(comparator_3_eq));  // open: gt, lt
  Comparator #(.width(4)) comparator_4 (.a(register_4_q), .b(4'b0000), .eq(comparator_4_eq));  // open: gt, lt
  and and_2 (out_7, not_3_out, Clock);
  and and_3 (out_9, not_4_out, Clock);
  not not_5 (not_5_out, comparator_4_eq);
  and and_4 (out_10, not_5_out, Clock);
endmodule

module Money_Input (
  input  Reset,
  input  _1,
  input  _5,
  input  _10,
  input  _25,
  input  _50,
  input  _1_2,
  input  _5_2,
  input  _10_2,
  input  _20,
  output [11:0] out_11,
  output [11:0] out_12
);

  wire n12_bit_super_adder_1_p12;
  wire [10:10] comparator_1_gt;
  wire [11:0] adder_1_out, n12_bit_super_adder_1_p11, register_1_q, subtractor_1_out;

  // Boba_Vending_Machine__Most_Recent__12_bit_super_adder 12_bit_super_adder_1: pin names not known; wires that end beside it: {12{1'b0}}, {{11{1'b0}}, _1}, {{9{1'b0}}, _5, 1'b0, _5}, {{8{1'b0}}, _10, 1'b0, _10, 1'b0}, {{7{1'b0}}, {2{_25}}, 2'b00, _25}, {{6{1'b0}}, {2{_50}}, 2'b00, _50, 1'b0}, {{5{1'b0}}, {2{_1_2}}, 2'b00, _1_2, 2'b00}, {3'b000, {5{_5_2}}, 1'b0, _5_2, 2'b00}, {2'b00, {5{_10_2}}, 1'b0, _10_2, 3'b000}, {1'b0, {5{_20}}, 1'b0, _20, 4'b0000}, n12_bit_super_adder_1_p11, n12_bit_super_adder_1_p12, 1'b1
  Adder #(.width(12)) adder_1 (.a(n12_bit_super_adder_1_p11), .b(register_1_q), .out(adder_1_out));  // open: cin, cout
  // Boba_Vending_Machine__Most_Recent__12_bit_super_adder 12_bit_super_adder_2: pin names not known
  Register #(.width(12)) register_1 (
    .D(adder_1_out), .Q(register_1_q), .clk(n12_bit_super_adder_1_p12), .clr(Reset));  // open: en
  Comparator #(.width(12), .mode("unsigned")) comparator_1 (
    .a(register_1_q), .b(12'h7d0), .gt(comparator_1_gt[10]));  // open: eq, lt
  Subtractor #(.width(12)) subtractor_1 (
    .a(register_1_q), .b({1'b0, {5{comparator_1_gt[10]}}, 1'b0, comparator_1_gt[10], 4'b0000}),
    .out(subtractor_1_out));  // open: bin, bout
  and and_1 (out_12[0], comparator_1_gt[10], subtractor_1_out[0]);
  and and_2 (out_12[1], comparator_1_gt[10], subtractor_1_out[1]);
  and and_3 (out_12[2], comparator_1_gt[10], subtractor_1_out[2]);
  and and_4 (out_12[3], comparator_1_gt[10], subtractor_1_out[3]);
  and and_5 (out_12[4], comparator_1_gt[10], subtractor_1_out[4]);
  and and_6 (out_12[5], comparator_1_gt[10], subtractor_1_out[5]);
  and and_7 (out_12[6], comparator_1_gt[10], subtractor_1_out[6]);
  and and_8 (out_12[7], comparator_1_gt[10], subtractor_1_out[7]);
  and and_9 (out_12[8], comparator_1_gt[10], subtractor_1_out[8]);
  and and_10 (out_12[9], comparator_1_gt[10], subtractor_1_out[9]);
  and and_11 (out_12[10], comparator_1_gt[10], subtractor_1_out[10]);
  and and_12 (out_12[11], comparator_1_gt[10], subtractor_1_out[11]);
  // Boba_Vending_Machine__Most_Recent__Merge_Balance_Output merge_balance_output_1: pin names not known; wires that end beside it: comparator_1_gt[10], register_1_q[0], out_11[0]
  // Boba_Vending_Machine__Most_Recent__Merge_Balance_Output merge_balance_output_2: pin names not known; wires that end beside it: comparator_1_gt[10], register_1_q[1], out_11[1]
  // Boba_Vending_Machine__Most_Recent__Merge_Balance_Output merge_balance_output_3: pin names not known; wires that end beside it: comparator_1_gt[10], register_1_q[2], out_11[2]
  // Boba_Vending_Machine__Most_Recent__Merge_Balance_Output merge_balance_output_4: pin names not known; wires that end beside it: comparator_1_gt[10], register_1_q[3], out_11[3]
  or or_1 (out_11[4], comparator_1_gt[10], register_1_q[4]);
  // Boba_Vending_Machine__Most_Recent__Merge_Balance_Output merge_balance_output_5: pin names not known; wires that end beside it: comparator_1_gt[10], register_1_q[5], out_11[5]
  or or_2 (out_11[6], comparator_1_gt[10], register_1_q[6]);
  or or_3 (out_11[7], comparator_1_gt[10], register_1_q[7]);
  or or_4 (out_11[8], comparator_1_gt[10], register_1_q[8]);
  or or_5 (out_11[9], comparator_1_gt[10], register_1_q[9]);
  or or_6 (out_11[10], comparator_1_gt[10], register_1_q[10]);
  Merge_Balance_Output merge_balance_output_6 (.R(comparator_1_gt[10]), .O20(register_1_q[11]), .O(out_11[11]));
endmodule

module Merge_Balance_Output (
  input  R,
  input  O20,
  output O
);

  wire not_1_out;

  and and_1 (O, R, not_1_out);
  not not_1 (not_1_out, O20);
endmodule

module Coin_Dispense (
  input  [3:0] How_many_1,
  input  in_2,
  input  Clock,
  output out_4,
  output out_5
);

  wire not_2_out;
  wire [0:0] not_1_out;
  wire [3:0] multiplexer_1_out, register_1_q, subtractor_1_out;

  Multiplexer #(.width(4)) multiplexer_1 (
    .in0(register_1_q), .in1(How_many_1), .out(multiplexer_1_out), .sel(out_4), .en(1'b1));
  not not_1 (not_1_out[0], out_4);
  Subtractor #(.width(4)) subtractor_1 (
    .a(multiplexer_1_out), .b({3'b000, not_1_out[0]}), .out(subtractor_1_out));  // open: bin, bout
  Register #(.width(4)) register_1 (.D(subtractor_1_out), .en(1'b1), .Q(register_1_q), .clk(Clock), .clr(in_2));
  Comparator #(.width(4)) comparator_1 (.a(register_1_q), .b(4'b0000), .eq(out_4));  // open: gt, lt
  not not_2 (not_2_out, out_4);
  and and_1 (out_5, not_2_out, Clock);
endmodule
